# Fritzing sketch raingauge (saved by Fritzing 0.9.3b)
breadboards: 1

parts:
  IC1 = DIP - 6 pins [chip_label=IC package="DIP (Dual Inline) [THT]"]
  R2 = Resistor [tolerance=±5% resistance=4.7k package=THT]
  S3 = Momentary Switch [package=ksa_sealed_tac_switch]
  R1 = Resistor [tolerance=±10% resistance=4.7k package=THT]
  S1 = Reed switch [package=THT]
  Raspberry_Pi_1 = Raspberry Pi 3 [part_number=RPI-3-V1.2]
  S4 = Pushbutton [package="[THT]"]
  R3 = Resistor [tolerance=±5% resistance=4.7k package=THT]
  LED1 = LED - 5mm [color="Red (633nm)" package="5 mm [THT]"]
  R4 = Resistor [tolerance=±5% resistance=470 package=THT]

nets:
  GND: IC1.GND, R2.Pin_0, R1.Pin_0, Raspberry_Pi_1.GND, R3.Pin_0, R4.Pin_0
  N1: IC1.SCL, Raspberry_Pi_1.GPIO3
  N2: IC1.SDA, Raspberry_Pi_1.GPIO2
  3V3: IC1.3V3, S3.1, S1.pin_2, Raspberry_Pi_1.3V3, S4.Pin_1, S4.Pin_2
  N3: R2.Pin_1, S3.3, Raspberry_Pi_1.GIPO22
  N4: R1.Pin_1, S1.pin_1, Raspberry_Pi_1.GIPO4, LED1.anode
  N5: Raspberry_Pi_1.GIPO21, S4.Pin_3, S4.Pin_4, R3.Pin_1
  N6: LED1.cathode, R4.Pin_1

custom parts:
  DIP - 6 pins: A DIP stand-in part for whatever IC you want. With 6 pins on a 300mil dual inline package (DIP) footprint.
